// Logisim project ULA.circ as structural Verilog
module meiosomador (
  input  in_1,
  input  in_2,
  output out_3,
  output out_4
);

  xor Soma (out_3, in_1, in_2);
  and Carry_In (out_4, in_1, in_2);
endmodule

module somadorcompleto (
  input  Cin,
  input  A,
  input  B,
  output \Saída_Soma ,
  output Cout
);

  wire A___B_out, A___Cin_out, B__Cin_out, Soma_out;

  xor Soma (Soma_out, A, B);
  and A___B (A___B_out, A, B);
  and A___Cin (A___Cin_out, A, Cin);
  and B__Cin (B__Cin_out, B, Cin);
  xor plus_Cin (\Saída_Soma , Cin, Soma_out);
  or Out (Cout, A___B_out, A___Cin_out, B__Cin_out);
endmodule

module MUX32 (
  input  E0,
  input  E1,
  input  E2,
  input  E3,
  input  E4,
  input  E5,
  input  E6,
  input  E7,
  input  E8,
  input  E9,
  input  E10,
  input  E11,
  input  E12,
  input  E13,
  input  E14,
  input  E15,
  input  E16,
  input  E17,
  input  E18,
  input  E19,
  input  E20,
  input  E21,
  input  E22,
  input  E23,
  input  E24,
  input  E25,
  input  E26,
  input  E27,
  input  E28,
  input  E29,
  input  E30,
  input  E31,
  input  [4:0] in_33,
  output out_34
);

  wire mux16_1_out_21, mux16_2_out_21;

  MUX16 mux16_1 (
    .E0(E0), .E1(E1), .E2(E2), .E3(E3), .in_5(E4), .E5(E5), .E6(E6), .E7(E7), .E8(E8), .E9(E9), .E10(E10),
    .E11(E11), .in_13(E12), .E13(E13), .E14(E14), .E15(E15), .C(in_33[3]), .D(in_33[2]), .A(in_33[1]),
    .B(in_33[0]), .out_21(mux16_1_out_21));
  MUX16 mux16_2 (
    .E0(E16), .E1(E17), .E2(E18), .E3(E19), .in_5(E20), .E5(E21), .E6(E22), .E7(E23), .E8(E24), .E9(E25),
    .E10(E26), .E11(E27), .in_13(E28), .E13(E29), .E14(E30), .E15(E31), .C(in_33[3]), .D(in_33[2]),
    .A(in_33[1]), .B(in_33[0]), .out_21(mux16_2_out_21));
  MUX2 mux2_1 (.E0(mux16_1_out_21), .E1(mux16_2_out_21), .E(in_33[4]), .out_4(out_34));
endmodule

module MUX4 (
  input  in_1,
  input  in_2,
  input  in_3,
  input  in_4,
  input  in_5,
  input  in_6,
  output out_7
);

  wire and_1_out, and_2_out, and_3_out, and_4_out;

  and and_1 (and_1_out, in_1, ~in_5, ~in_6);  // AND_Gate
  and and_2 (and_2_out, in_2, ~in_5, in_6);  // AND_Gate
  and and_3 (and_3_out, in_3, in_5, ~in_6);  // AND_Gate
  and and_4 (and_4_out, in_4, in_5, in_6);
  or or_1 (out_7, and_1_out, and_2_out, and_3_out, and_4_out);
endmodule

module MUX16 (
  input  E0,
  input  E1,
  input  E2,
  input  E3,
  input  in_5,
  input  E5,
  input  E6,
  input  E7,
  input  E8,
  input  E9,
  input  E10,
  input  E11,
  input  in_13,
  input  E13,
  input  E14,
  input  E15,
  input  C,
  input  D,
  input  A,
  input  B,
  output out_21
);

  wire mux8_1_out_12, mux8_2_out_12;

  MUX8 mux8_1 (
    .E0(E0), .E1(E1), .E2(E2), .E3(E3), .E4(in_5), .E5(E5), .E6(E6), .E7(E7), .B(D), .C(A), .A(B),
    .out_12(mux8_1_out_12));
  MUX8 mux8_2 (
    .E0(E8), .E1(E9), .E2(E10), .E3(E11), .E4(in_13), .E5(E13), .E6(E14), .E7(E15), .B(D), .C(A), .A(B),
    .out_12(mux8_2_out_12));
  MUX2 mux2_1 (.E0(mux8_1_out_12), .E1(mux8_2_out_12), .E(C), .out_4(out_21));
endmodule

module MUX2 (
  input  E0,
  input  E1,
  input  E,
  output out_4
);

  wire and_1_out, and_2_out;

  and and_1 (and_1_out, E0, ~E);  // AND_Gate
  and and_2 (and_2_out, E1, E);
  or or_1 (out_4, and_1_out, and_2_out);
endmodule

module \CélulaULA  (
  input  A,
  input  B,
  input  Cin,
  input  [4:0] in_4,
  output Cout,
  output \Saída 
);

  wire and_1_out, nand_1_out, or_1_out, \somadorcompleto_1_saída_soma , xor_1_out;

  and and_1 (and_1_out, A, B);
  or or_1 (or_1_out, A, B);
  xor xor_1 (xor_1_out, A, B);
  somadorcompleto somadorcompleto_1 (
    .Cin(Cin), .A(A), .B(B), .\Saída_Soma (\somadorcompleto_1_saída_soma ), .Cout(Cout));
  nand nand_1 (nand_1_out, ~A, B);  // NAND_Gate
  MUX32 mux32_1 (
    .E0(and_1_out), .E1(or_1_out), .E2(\somadorcompleto_1_saída_soma ), .E3(xor_1_out), .E4(B), .E5(B),
    .E6(B), .E7(B), .E8(B), .E9(B), .E10(B), .E11(B), .E12(B), .E13(nand_1_out), .E14(nand_1_out),
    .E15(nand_1_out), .E16(nand_1_out), .E17(nand_1_out), .E18(nand_1_out), .E19(nand_1_out),
    .E20(nand_1_out), .E21(nand_1_out), .E22(nand_1_out), .E23(nand_1_out), .E24(nand_1_out),
    .E25(nand_1_out), .E26(nand_1_out), .E27(nand_1_out), .E28(nand_1_out), .E29(nand_1_out),
    .E30(nand_1_out), .E31(nand_1_out), .in_33(in_4), .out_34(\Saída ));
endmodule

module ULA (
  input  [31:0] in_1,
  input  [31:0] in_2,
  input  [4:0] OpCode,
  output out_4,
  output \SaídaDetector ,
  output [31:0] out_6
);

  wire \célulaula_1_cout , \célulaula_3_cout , \célulaula_4_cout , \célulaula_5_cout , \célulaula_6_cout ,
       \célulaula_7_cout , \célulaula_8_cout , \célulaula_9_cout , \célulaula_10_cout , \célulaula_11_cout ,
       \célulaula_12_cout , \célulaula_13_cout , \célulaula_14_cout , \célulaula_15_cout ,
       \célulaula_16_cout , \célulaula_17_cout , \célulaula_18_cout , \célulaula_19_cout ,
       \célulaula_20_cout , \célulaula_21_cout , \célulaula_22_cout , \célulaula_23_cout ,
       \célulaula_24_cout , \célulaula_25_cout , \célulaula_26_cout , \célulaula_27_cout ,
       \célulaula_28_cout , \célulaula_29_cout , \célulaula_30_cout , \célulaula_31_cout ,
       \célulaula_32_cout , extra1detect_1_out_2, extra2detect_1_out_2, slldetect_1_out_2;
  wire [31:0] shiftleftlogico_1_out_3, shiftrightarit_1_out_3, shiftrightlogico_1_out_3;

  ShiftRightLogico shiftrightlogico_1 (
    .in_1(shiftleftlogico_1_out_3), .in_2(extra1detect_1_out_2), .out_3(shiftrightlogico_1_out_3));
  ShiftLeftLogico shiftleftlogico_1 (.in_1(in_2), .in_2(slldetect_1_out_2), .out_3(shiftleftlogico_1_out_3));
  extra1Detect extra1detect_1 (.in_1(OpCode), .out_2(extra1detect_1_out_2));
  SLLDetect slldetect_1 (.in_1(OpCode), .out_2(slldetect_1_out_2));
  ShiftRightArit shiftrightarit_1 (
    .in_1(shiftrightlogico_1_out_3), .Shift(extra2detect_1_out_2), .out_3(shiftrightarit_1_out_3));
  extra2Detect extra2detect_1 (.in_1(OpCode), .out_2(extra2detect_1_out_2));
  \CélulaULA  \célulaula_1  (
    .Cout(\célulaula_1_cout ), .Cin(\célulaula_4_cout ), .\Saída (out_6[30]), .A(in_1[30]),
    .B(shiftrightarit_1_out_3[30]), .in_4(OpCode));
  \CélulaULA  \célulaula_2  (
    .Cout(out_4), .Cin(\célulaula_1_cout ), .\Saída (out_6[31]), .A(in_1[31]),
    .B(shiftrightarit_1_out_3[31]), .in_4(OpCode));
  \CélulaULA  \célulaula_3  (
    .Cout(\célulaula_3_cout ), .Cin(\célulaula_6_cout ), .\Saída (out_6[28]), .A(in_1[28]),
    .B(shiftrightarit_1_out_3[28]), .in_4(OpCode));
  \CélulaULA  \célulaula_4  (
    .Cout(\célulaula_4_cout ), .Cin(\célulaula_3_cout ), .\Saída (out_6[29]), .A(in_1[29]),
    .B(shiftrightarit_1_out_3[29]), .in_4(OpCode));
  \CélulaULA  \célulaula_5  (
    .Cout(\célulaula_5_cout ), .Cin(\célulaula_8_cout ), .\Saída (out_6[26]), .A(in_1[26]),
    .B(shiftrightarit_1_out_3[26]), .in_4(OpCode));
  \CélulaULA  \célulaula_6  (
    .Cout(\célulaula_6_cout ), .Cin(\célulaula_5_cout ), .\Saída (out_6[27]), .A(in_1[27]),
    .B(shiftrightarit_1_out_3[27]), .in_4(OpCode));
  \CélulaULA  \célulaula_7  (
    .Cout(\célulaula_7_cout ), .Cin(\célulaula_10_cout ), .\Saída (out_6[24]), .A(in_1[24]),
    .B(shiftrightarit_1_out_3[24]), .in_4(OpCode));
  \CélulaULA  \célulaula_8  (
    .Cout(\célulaula_8_cout ), .Cin(\célulaula_7_cout ), .\Saída (out_6[25]), .A(in_1[25]),
    .B(shiftrightarit_1_out_3[25]), .in_4(OpCode));
  \CélulaULA  \célulaula_9  (
    .Cout(\célulaula_9_cout ), .Cin(\célulaula_11_cout ), .\Saída (out_6[22]), .A(in_1[22]),
    .B(shiftrightarit_1_out_3[22]), .in_4(OpCode));
  \CélulaULA  \célulaula_10  (
    .Cout(\célulaula_10_cout ), .Cin(\célulaula_9_cout ), .\Saída (out_6[23]), .A(in_1[23]),
    .B(shiftrightarit_1_out_3[23]), .in_4(OpCode));
  \CélulaULA  \célulaula_11  (
    .Cout(\célulaula_11_cout ), .Cin(\célulaula_12_cout ), .\Saída (out_6[21]), .A(in_1[21]),
    .B(shiftrightarit_1_out_3[21]), .in_4(OpCode));
  \CélulaULA  \célulaula_12  (
    .Cout(\célulaula_12_cout ), .Cin(\célulaula_13_cout ), .\Saída (out_6[20]), .A(in_1[20]),
    .B(shiftrightarit_1_out_3[20]), .in_4(OpCode));
  \CélulaULA  \célulaula_13  (
    .Cout(\célulaula_13_cout ), .Cin(\célulaula_14_cout ), .\Saída (out_6[19]), .A(in_1[19]),
    .B(shiftrightarit_1_out_3[19]), .in_4(OpCode));
  \CélulaULA  \célulaula_14  (
    .Cout(\célulaula_14_cout ), .Cin(\célulaula_16_cout ), .\Saída (out_6[18]), .A(in_1[18]),
    .B(shiftrightarit_1_out_3[18]), .in_4(OpCode));
  \CélulaULA  \célulaula_15  (
    .Cout(\célulaula_15_cout ), .Cin(\célulaula_17_cout ), .\Saída (out_6[16]), .A(in_1[16]),
    .B(shiftrightarit_1_out_3[16]), .in_4(OpCode));
  \CélulaULA  \célulaula_16  (
    .Cout(\célulaula_16_cout ), .Cin(\célulaula_15_cout ), .\Saída (out_6[17]), .A(in_1[17]),
    .B(shiftrightarit_1_out_3[17]), .in_4(OpCode));
  \CélulaULA  \célulaula_17  (
    .Cout(\célulaula_17_cout ), .Cin(\célulaula_18_cout ), .\Saída (out_6[15]), .A(in_1[15]),
    .B(shiftrightarit_1_out_3[15]), .in_4(OpCode));
  \CélulaULA  \célulaula_18  (
    .Cout(\célulaula_18_cout ), .Cin(\célulaula_19_cout ), .\Saída (out_6[14]), .A(in_1[14]),
    .B(shiftrightarit_1_out_3[14]), .in_4(OpCode));
  \CélulaULA  \célulaula_19  (
    .Cout(\célulaula_19_cout ), .Cin(\célulaula_20_cout ), .\Saída (out_6[13]), .A(in_1[13]),
    .B(shiftrightarit_1_out_3[13]), .in_4(OpCode));
  \CélulaULA  \célulaula_20  (
    .Cout(\célulaula_20_cout ), .Cin(\célulaula_22_cout ), .\Saída (out_6[12]), .A(in_1[12]),
    .B(shiftrightarit_1_out_3[12]), .in_4(OpCode));
  \CélulaULA  \célulaula_21  (
    .Cout(\célulaula_21_cout ), .Cin(\célulaula_24_cout ), .\Saída (out_6[10]), .A(in_1[10]),
    .B(shiftrightarit_1_out_3[10]), .in_4(OpCode));
  \CélulaULA  \célulaula_22  (
    .Cout(\célulaula_22_cout ), .Cin(\célulaula_21_cout ), .\Saída (out_6[11]), .A(in_1[11]),
    .B(shiftrightarit_1_out_3[11]), .in_4(OpCode));
  \CélulaULA  \célulaula_23  (
    .Cout(\célulaula_23_cout ), .Cin(\célulaula_25_cout ), .\Saída (out_6[8]), .A(in_1[8]),
    .B(shiftrightarit_1_out_3[8]), .in_4(OpCode));
  \CélulaULA  \célulaula_24  (
    .Cout(\célulaula_24_cout ), .Cin(\célulaula_23_cout ), .\Saída (out_6[9]), .A(in_1[9]),
    .B(shiftrightarit_1_out_3[9]), .in_4(OpCode));
  \CélulaULA  \célulaula_25  (
    .Cout(\célulaula_25_cout ), .Cin(\célulaula_26_cout ), .\Saída (out_6[7]), .A(in_1[7]),
    .B(shiftrightarit_1_out_3[7]), .in_4(OpCode));
  \CélulaULA  \célulaula_26  (
    .Cout(\célulaula_26_cout ), .Cin(\célulaula_28_cout ), .\Saída (out_6[6]), .A(in_1[6]),
    .B(shiftrightarit_1_out_3[6]), .in_4(OpCode));
  \CélulaULA  \célulaula_27  (
    .Cout(\célulaula_27_cout ), .Cin(\célulaula_30_cout ), .\Saída (out_6[4]), .A(in_1[4]),
    .B(shiftrightarit_1_out_3[4]), .in_4(OpCode));
  \CélulaULA  \célulaula_28  (
    .Cout(\célulaula_28_cout ), .Cin(\célulaula_27_cout ), .\Saída (out_6[5]), .A(in_1[5]),
    .B(shiftrightarit_1_out_3[5]), .in_4(OpCode));
  \CélulaULA  \célulaula_29  (
    .Cout(\célulaula_29_cout ), .Cin(\célulaula_32_cout ), .\Saída (out_6[2]), .A(in_1[2]),
    .B(shiftrightarit_1_out_3[2]), .in_4(OpCode));
  \CélulaULA  \célulaula_30  (
    .Cout(\célulaula_30_cout ), .Cin(\célulaula_29_cout ), .\Saída (out_6[3]), .A(in_1[3]),
    .B(shiftrightarit_1_out_3[3]), .in_4(OpCode));
  \CélulaULA  \célulaula_31  (
    .Cout(\célulaula_31_cout ), .Cin(1'b0), .\Saída (out_6[0]), .A(in_1[0]), .B(shiftrightarit_1_out_3[0]),
    .in_4(OpCode));
  \CélulaULA  \célulaula_32  (
    .Cout(\célulaula_32_cout ), .Cin(\célulaula_31_cout ), .\Saída (out_6[1]), .A(in_1[1]),
    .B(shiftrightarit_1_out_3[1]), .in_4(OpCode));
  nor nor_1 (\SaídaDetector , out_6[0], out_6[1], out_6[2], out_6[3], out_6[4], out_6[5], out_6[6], out_6[7], out_6[8], out_6[9], out_6[10], out_6[11], out_6[12], out_6[13], out_6[14], out_6[15], out_6[16], out_6[17], out_6[18], out_6[19], out_6[20], out_6[21], out_6[22], out_6[23], out_6[24], out_6[25], out_6[26], out_6[27], out_6[28], out_6[29], out_6[30], out_6[31]);
endmodule

module MUX8 (
  input  E0,
  input  E1,
  input  E2,
  input  E3,
  input  E4,
  input  E5,
  input  E6,
  input  E7,
  input  B,
  input  C,
  input  A,
  output out_12
);

  wire mux4_1_out_7, mux4_2_out_7;

  MUX4 mux4_1 (.in_1(E0), .in_2(E1), .in_3(E2), .in_4(E3), .in_5(C), .in_6(A), .out_7(mux4_1_out_7));
  MUX4 mux4_2 (.in_1(E4), .in_2(E5), .in_3(E6), .in_4(E7), .in_5(C), .in_6(A), .out_7(mux4_2_out_7));
  MUX2 mux2_1 (.E0(mux4_1_out_7), .E1(mux4_2_out_7), .E(B), .out_4(out_12));
endmodule

module ShiftLeftLogico (
  input  [31:0] in_1,
  input  in_2,
  output [31:0] out_3
);

  MUX2maisbits mux2maisbits_1 (.E0(in_1), .E1({in_1[30:0], 1'b0}), .E(in_2), .out_4(out_3));
endmodule

module MUX2maisbits (
  input  [31:0] E0,
  input  [31:0] E1,
  input  E,
  output [31:0] out_4
);

  wire [31:0] and_1_out, and_2_out;

  assign and_1_out = E0 & ~{32{E}};  // AND_Gate and_1, 32 bits wide
  assign and_2_out = E1 & {32{E}};  // AND_Gate and_2, 32 bits wide
  assign out_4 = and_1_out | and_2_out;  // OR_Gate or_1, 32 bits wide
endmodule

module ShiftRightLogico (
  input  [31:0] in_1,
  input  in_2,
  output [31:0] out_3
);

  MUX2maisbits mux2maisbits_1 (.E0(in_1), .E1({1'b0, in_1[31:1]}), .E(in_2), .out_4(out_3));
endmodule

module ShiftRightArit (
  input  [31:0] in_1,
  input  Shift,
  output [31:0] out_3
);

  MUX2maisbits mux2maisbits_1 (.E0(in_1), .E1({{2{in_1[31]}}, in_1[30:1]}), .E(Shift), .out_4(out_3));
endmodule

module ShiftLeftArit (
  input  [31:0] in_1,
  input  in_2,
  output [31:0] out_3
);

  MUX2maisbits mux2maisbits_1 (.E0(in_1), .E1({in_1[30:0], in_1[0]}), .E(in_2), .out_4(out_3));
endmodule

module SLLDetect (
  input  [4:0] in_1,
  output out_2
);

  and and_1 (out_2, ~in_1[0], ~in_1[1], in_1[2], ~in_1[3], ~in_1[4]);  // AND_Gate

  // Notes on the sheet:
  //   00000 = and
  //   00001 = or
  //   00010 = soma
  //   00011 = xor
  //   00100 = sll
endmodule

module ANDDetect (
  input  [4:0] in_1,
  output out_2
);

  and and_1 (out_2, ~in_1[0], ~in_1[1], ~in_1[2], ~in_1[3], ~in_1[4]);  // AND_Gate
endmodule

module ORDetect (
  input  [4:0] in_1,
  output out_2
);

  and and_1 (out_2, in_1[0], ~in_1[1], ~in_1[2], ~in_1[3], ~in_1[4]);  // AND_Gate
endmodule

module SOMADetect (
  input  [4:0] in_1,
  output out_2
);

  and and_1 (out_2, ~in_1[0], in_1[1], ~in_1[2], ~in_1[3], ~in_1[4]);  // AND_Gate
endmodule

module XORDETECT (
  input  [4:0] in_1,
  output out_2
);

  and and_1 (out_2, in_1[0], in_1[1], ~in_1[2], ~in_1[3], ~in_1[4]);  // AND_Gate
endmodule

module extra1Detect (
  input  [4:0] in_1,
  output out_2
);

  and and_1 (out_2, in_1[0], ~in_1[1], in_1[2], ~in_1[3], ~in_1[4]);  // AND_Gate
endmodule

module extra2Detect (
  input  [4:0] in_1,
  output out_2
);

  and and_1 (out_2, ~in_1[0], in_1[1], in_1[2], ~in_1[3], ~in_1[4]);  // AND_Gate
endmodule

module extra3Detect (
  input  [4:0] in_1,
  output out_2
);

  and and_1 (out_2, in_1[0], in_1[1], in_1[2], ~in_1[3], ~in_1[4]);  // AND_Gate
endmodule

module extra4Detect (
  input  [4:0] in_1,
  output out_2
);

  and and_1 (out_2, ~in_1[0], ~in_1[1], ~in_1[2], in_1[3], ~in_1[4]);  // AND_Gate
endmodule

module extra5Detect (
  input  [4:0] in_1,
  output out_2
);

  and and_1 (out_2, in_1[0], ~in_1[1], ~in_1[2], in_1[3], ~in_1[4]);  // AND_Gate
endmodule

module extra6Detect (
  input  [4:0] in_1,
  output out_2
);

  and and_1 (out_2, ~in_1[0], in_1[1], ~in_1[2], in_1[3], ~in_1[4]);  // AND_Gate
endmodule

module extra7Detecy (
  input  [4:0] in_1,
  output out_2
);

  and and_1 (out_2, in_1[0], in_1[1], ~in_1[2], in_1[3], ~in_1[4]);  // AND_Gate
endmodule

module extra8Detect (
  input  [4:0] in_1,
  output out_2
);

  and and_1 (out_2, ~in_1[0], ~in_1[1], in_1[2], in_1[3], ~in_1[4]);  // AND_Gate
endmodule

module extra9Detect (
  input  [4:0] in_1,
  output out_2
);

  and and_1 (out_2, in_1[0], ~in_1[1], in_1[2], in_1[3], ~in_1[4]);  // AND_Gate
endmodule

module extra10Detect (
  input  [4:0] in_1,
  output out_2
);

  and and_1 (out_2, ~in_1[0], in_1[1], in_1[2], in_1[3], ~in_1[4]);  // AND_Gate
endmodule

module extra11Detect (
  input  [4:0] in_1,
  output out_2
);

  and and_1 (out_2, in_1[0], in_1[1], in_1[2], in_1[3], ~in_1[4]);  // AND_Gate
endmodule

module ULAdesenho (
);

  ULA ula_1 ();  // open: in_1, in_2, out_4, OpCode, SaídaDetector, out_6
endmodule
