// Logisim project teste.circ as structural Verilog: 4 circuits, main circuit main
module main (
  input  in_1,
  input  in_2,
  output out_3,
  output out_4
);

  and and_1 (out_3, in_1, in_2);
  or or_1 (out_4, in_1, in_2);
endmodule

module mux2 (
  input  A,
  input  B,
  input  in_3,
  output out_4
);

  wire and_1_out, and_2_out;

  and and_1 (and_1_out, A, ~in_3);  // AND_Gate
  and and_2 (and_2_out, B, in_3);
  or or_1 (out_4, and_1_out, and_2_out);
endmodule

module MUX4 (
  input  A,
  input  B,
  input  C,
  input  D,
  input  in_5,
  input  in_6,
  output out_7
);

  wire mux2_1_out_4, mux2_2_out_4;

  mux2 mux2_1 (.A(A), .B(B), .in_3(in_6), .out_4(mux2_1_out_4));
  mux2 mux2_2 (.A(C), .B(D), .in_3(in_6), .out_4(mux2_2_out_4));
  mux2 mux2_3 (.A(mux2_1_out_4), .B(mux2_2_out_4), .in_3(in_5), .out_4(out_7));
endmodule

module mux4b (
  input  in_1,
  input  in_2,
  input  in_3,
  input  in_4,
  input  [1:0] in_5,
  input  [1:0] in_6,
  output out_7,
  output out_8,
  output out_9
);

  wire and_1_out, and_2_out, and_3_out, and_4_out;

  and and_1 (and_1_out, in_1, ~in_5[1], ~in_5[0]);  // AND_Gate
  and and_2 (and_2_out, in_2, ~in_5[1], in_5[0]);  // AND_Gate
  and and_3 (and_3_out, in_3, in_5[1], ~in_5[0]);  // AND_Gate
  and and_4 (and_4_out, in_4, in_5[1], in_5[0]);
  or or_1 (out_7, and_1_out, and_2_out, and_3_out, and_4_out);

  assign out_8 = in_6[0];
  assign out_9 = in_6[1];
endmodule
